# Fritzing sketch ProjOIC (saved by Fritzing 0.9.4)
breadboards: 1

parts:
  Componente1 = Logic Level Converter
  VCC1 = 4 x AAA Battery Mount
  KY-1 = Keyes Relay [package=THT]
  M1 = DC Motor
  Componente2 = FC-28 Soil Hygrometer Module - Probe
  Componente3 = FC-28 Soil Hygrometer Module
  U2 = NodeMCU V1.0

nets:
  VCC: Componente1.LV, Componente3.VCC, U2.3V3
  N1: Componente1.TX_LV, U2.D1
  N2: Componente1.TX_HV, KY-1.signal
  N3: Componente1.HV, KY-1.power, U2.Vin
  GND: Componente1.GND, KY-1.ground, Componente3.GND, U2.GND
  N4: VCC1.+, KY-1.C
  N5: KY-1.NO, M1.pin_1
  N6: Componente2.POS, Componente3.POS
  N7: Componente2.NEG, Componente3.NEG
  N8: Componente3.AO, U2.A0

custom parts:
  Keyes Relay: The Keyes 5V relay module is suitable for SCM development, home appliance control. It uses a 5V~12V TIL control signal which can control DC / AC signal.
  FC-28 Soil Hygrometer Module - Probe: The FC-28 is a soil hygrometer module that uses the Texas Instruments LM393 comparator chip to provide an analog measurement of soil humidity.
  FC-28 Soil Hygrometer Module: The FC-28 is a soil hygrometer module that uses the Texas Instruments LM393 comparator chip to provide an analog measurement of soil humidity. The digital output is high when soil moisture is over a certain threshold, as determined by adjusting the potentiometer.
  NodeMCU V1.0: ESP8266 based NodeMCU
